# Fritzing sketch ultrasonic (saved by Fritzing 0.9.2b)
breadboards: 1

parts:
  J1 = Infrared Proximity Sensor
  Part1 = Arduino Uno (Rev3)
  LED1 = LED - 5mm [color="Green (570nm)" package="5 mm [THT]"]
  R1 = Resistor [tolerance=±5% resistance=220 package=THT]

nets:
  N1: J1.Vout, Part1.D2
  N2: J1.GND, Part1.D3_PWM
  VCC: J1.Vcc, Part1.5V
  N3: Part1.D9_PWM, LED1.anode
  N4: Part1.GND, R1.Pin_0
  N5: LED1.cathode, R1.Pin_1
